# Fritzing sketch SignalTower (saved by Fritzing 0.7.10b)

parts:
  Arduino1 = Arduino
  LED1 = LED - 5mm [color="Red (633nm)" package="5 mm [THT]"]

nets:
  N1: Arduino1.GND, LED1.cathode
  N2: Arduino1.D13, LED1.anode
